# Fritzing sketch circuit_diagram (saved by Fritzing 1.0.2b)

parts:
  M1 = RioRand LM2596
  J1 = Screw terminal - 2 pins [package=THT]
  J2 = Screw terminal - 2 pins [package=THT]
  ZS-042_RTC1 = ZS-042 RTC Module
  4_Channel_Relay1 = 4 Channel Power Relay
  M2 = DOIT Esp32 DevKit v1 (30 pins long, 11 pins width) [part_number=ESP32S-PIN30]
  S1 = Pushbutton [package="[THT]"]
  R1 = Resistor [tolerance=±5% resistance=10k package="0402 [SMD]"]

nets:
  N1: M1.Pin_1, J1.pin2
  N2: M1.Pin_2, J1.pin1
  VCC: M1.Pin_3, J2.pin2, 4_Channel_Relay1.VCC, M2.VIN, S1.Pin_1, S1.Pin_2
  GND: M1.Pin_4, J2.pin1, ZS-042_RTC1.GND, 4_Channel_Relay1.GND, M2.GND, R1.Pin_0
  VCC_2: ZS-042_RTC1.VCC, M2.3V3
  N3: ZS-042_RTC1.SDA, M2.D15
  N4: ZS-042_RTC1.SCL, M2.D2
  N5: 4_Channel_Relay1.IN1, M2.D26
  N6: 4_Channel_Relay1.IN2, M2.D25
  N7: 4_Channel_Relay1.IN3, M2.D33
  N8: 4_Channel_Relay1.IN4, M2.D32
  N9: M2.D5, S1.Pin_3, S1.Pin_4, R1.Pin_1

custom parts:
  4 Channel Power Relay: A 4 channel power relay. The module operates at 5V.
  DOIT Esp32 DevKit v1 (30 pins long, 11 pins width): The DOIT Esp32 DevKit v1 is one of the development board created by DOIT to evaluate the ESP-WROOM-32 module. It is based on the ESP32 microcontroller that boasts Wifi, Bluetooth, Ethernet and Low Power support all in a single chip. (vanepp) made breadboard work, adjusted pin numbering and labels and reduced size of schematic and cleaned up pcb. This chip is 30pins long (2 x15) and 11 pins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
